# Fritzing sketch Treppenbeleuchtung_Teil1 (saved by Fritzing 0.9.3b)
breadboards: 2

parts:
  Nano_V1 = Nano V3
  Bauteil1 = 16-Channel 12-bit PWM Servo Driver - I2C [part_number=815]
  Bauteil5 = IFR520 MOS module [package=THT]
  PIR1 = PIR sensor
  PIR2 = PIR sensor
  Bauteil6 = IFR520 MOS module [package=THT]
  LED1 = LEDs [package=led10mm]
  LED2 = LEDs [package=led10mm]
  YwRobot_Power_Supply1 = YwRobot Breadboard Power Supply [part_number=545043]

nets:
  GND: Nano_V1.GND, Bauteil1.GND, Bauteil5.GND, PIR1.GND, PIR2.GND, Bauteil6.GND, YwRobot_Power_Supply1.GND#13
  N1: Nano_V1.D2, PIR1.SIG
  N2: Nano_V1.D3, PIR2.SIG
  N3: Nano_V1.D8, Bauteil1.OE
  VCC: Nano_V1.5V, Bauteil1.VCC, Bauteil5.VCC, PIR1.VDD, PIR2.VDD, Bauteil6.VCC, YwRobot_Power_Supply1.VCC#9
  N4: Nano_V1.A5, Bauteil1.SCL
  N5: Nano_V1.A4, Bauteil1.SDA
  N6: Bauteil1.PWM1, Bauteil6.SIG
  N7: Bauteil1.PWM0, Bauteil5.SIG
  N8: Bauteil5.V+, Bauteil5.V-, LED1.A, LED1.C
  N9: Bauteil6.V+, LED2.A
  N10: Bauteil6.V-, LED2.C

custom parts:
  Nano V3: Can be used universally thanks to a compact design! By 14 digital in - and outputs and 6 analog inputs on the Nano V3 can also be used for larger projects! Thanks to the ATmega328 micro-controller, as well as more sophisticated programs to be executable! By Arduino compatibility in the Arduino IDE programmable! With FTDI Chip! Usual high quality and fast delivery directly from Germany by order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
  16-Channel 12-bit PWM Servo Driver - I2C: You want to make a cool robot, maybe a hexapod walker, or maybe just a piece of art with a lot of moving parts. Or maybe you want to drive a lot of LEDs with precise PWM output. Using only two pins, control 16 free-running PWM outputs! You can even chain up 62 breakouts to control up to 992 PWM outputs.
  LEDs: LEDs Standard schematic elements and footprints for 5mm, 3mm, 1206, and 0603 sized LEDs. 5mm - Spark Fun Electronics SKU : COM-00529 (and others)
  YwRobot Breadboard Power Supply: The YwRobot Breadboard Power Supply (MB-V2) has two power rails; they can be 5V or 3V3. Power to the module can be provided through the female USB socket or through the A10 (female) 2.1mm power jack.
